# Fritzing sketch BatLight Fritzing Sketch (saved by Fritzing 0.9.2b)
circuit board: 8.29574cm x 2.7102cm

parts:
  BUTTON1 = Arcade Button (red)
  BUTTON2 = Arcade Button (white)
  5V_2A = 2.1mm DC Barrel Jack
  Pro_Trinket_5V = Pro Trinket 5V
  NEOPIXEL1 = Neopixel Strip -- White (60/m)
  C1 = Electrolytic Capacitor [capacitance=1mF package="200 mil [THT, electrolytic]"]
  R1 = Resistor [tolerance=±5% resistance=470 package=THT]

nets:
  N1: BUTTON1.no_name_yet#1, Pro_Trinket_5V.D3
  GND: BUTTON1.no_name_yet#2, BUTTON2.no_name_yet#2, 5V_2A.sleeve, Pro_Trinket_5V.GND, NEOPIXEL1.GND, C1.-
  N2: BUTTON2.no_name_yet#1, Pro_Trinket_5V.D4
  N3: 5V_2A.center, Pro_Trinket_5V.VBAT, NEOPIXEL1.+5V, C1.+
  N4: Pro_Trinket_5V.D6, R1.Pin_1
  N5: NEOPIXEL1.DI, R1.Pin_0

custom parts:
  Arcade Button (red): Adafruit Arcade Button (red)
  Arcade Button (white): Adafruit Arcade Button (white)
  2.1mm DC Barrel Jack: 2.1mm DC Barrel Jack with Thru-Hole Connectors (breadboardable)
  Pro Trinket 5V: The Pro Trinket 5V is like an Arduino Pro Mini with more pins and USB included. Built with the common core Arduino chip, the ATmega328p, it has 18 GPIO, 2 extra analog inputs, 28K of flash, and 2K of RAM. It has onboard USB bootloading support with Optiboot support, so you can either program your Pro Trinket over USB or with a FTDI cable. The Pro Trinket is programmable using the Arduino IDE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
  Neopixel Strip -- White (60/m): Neopixel Strip, White, 60 pixels per meter.
